// Logisim project Elevator System.circ as structural Verilog: 4 circuits, main circuit main
module main (
  input  Outside,
  input  Inside
);

  wire _1st_floor_call_ff2_q, _1st_floor_call_ff_q, CALL_to_1st_out, Call_to_2nd_floor_ff2_q,
       call_to_2nd_floor_ff_q, CALL_to_2nd_out, CALL_to_floor_out, Clock_out, decoder_1_out0, decoder_1_out1,
       decoder_2_out0, decoder_2_out1, display_1_a, display_1_b, display_1_c, display_1_d, display_1_e,
       display_1_f, display_1_g, display_1_point, elevator_1_call_button, elevator_1_door,
       elevator_1_downward, elevator_1_floor1_2, elevator_1_floor2_2, elevator_1_ground_floor_2,
       elevator_1_upward, Floor0_q, Floor1_q, Floor2_q, floor_button_1_call_floor0,
       floor_button_1_call_floor1, floor_button_1_call_floor2, floor_button_1_go_floor0_signal,
       floor_button_1_go_floor1_signal, floor_button_1_go_floor2_signal, GO_1st_out, Go_2nd_out,
       GO_floor_out, Go_to_1st_floor_ff2_q, Go_to_1st_floor_ff_q, Go_to_2nd_floor_ff2_q,
       Go_to_2nd_floor_ff_q, Go_to_ground_ff2_q, Go_to_ground_ff_q, Ground_floor_ff2_q, Ground_Floor_ff_q,
       not_1_out, or_1_out, or_2_out, or_3_out, or_4_out, or_5_out, or_6_out;

  or or_1 (or_1_out, Ground_floor_ff2_q, Ground_Floor_ff_q);
  or or_2 (or_2_out, Call_to_2nd_floor_ff2_q, call_to_2nd_floor_ff_q);
  or or_3 (or_3_out, Go_to_1st_floor_ff2_q, Go_to_1st_floor_ff_q);
  Clock Clock (.out(Clock_out));
  D_Flip_Flop Floor0 (.clk(Clock_out), .D(elevator_1_ground_floor_2), .Q(Floor0_q));  // open: Qn, preset, en, reset
  D_Flip_Flop Floor1 (.clk(Clock_out), .D(elevator_1_floor1_2), .Q(Floor1_q));  // open: Qn, preset, en, reset
  D_Flip_Flop Floor2 (.clk(Clock_out), .D(elevator_1_floor2_2), .Q(Floor2_q));  // open: Qn, preset, en, reset
  D_Flip_Flop Ground_floor_ff2 (
    .clk(Clock_out), .D(Ground_Floor_ff_q), .Q(Ground_floor_ff2_q));  // open: Qn, preset, en, reset
  D_Flip_Flop Ground_Floor_ff (
    .clk(Clock_out), .D(floor_button_1_call_floor0), .Q(Ground_Floor_ff_q));  // open: Qn, preset, en, reset
  D_Flip_Flop Call_to_2nd_floor_ff2 (
    .clk(Clock_out), .D(call_to_2nd_floor_ff_q), .Q(Call_to_2nd_floor_ff2_q));  // open: Qn, preset, en, reset
  D_Flip_Flop call_to_2nd_floor_ff (
    .clk(Clock_out), .D(floor_button_1_call_floor2), .Q(call_to_2nd_floor_ff_q));  // open: Qn, preset, en, reset
  D_Flip_Flop Go_to_1st_floor_ff2 (
    .clk(Clock_out), .D(Go_to_1st_floor_ff_q), .Q(Go_to_1st_floor_ff2_q));  // open: Qn, preset, en, reset
  D_Flip_Flop Go_to_1st_floor_ff (
    .clk(Clock_out), .D(floor_button_1_go_floor1_signal), .Q(Go_to_1st_floor_ff_q));  // open: Qn, preset, en, reset
  D_Flip_Flop _1st_floor_call_ff2 (
    .clk(Clock_out), .D(_1st_floor_call_ff_q), .Q(_1st_floor_call_ff2_q));  // open: Qn, preset, en, reset
  or or_4 (or_4_out, _1st_floor_call_ff2_q, _1st_floor_call_ff_q);
  D_Flip_Flop _1st_floor_call_ff (
    .clk(Clock_out), .D(floor_button_1_call_floor1), .Q(_1st_floor_call_ff_q));  // open: Qn, preset, en, reset
  D_Flip_Flop Go_to_ground_ff2 (
    .clk(Clock_out), .D(Go_to_ground_ff_q), .Q(Go_to_ground_ff2_q));  // open: Qn, preset, en, reset
  or or_5 (or_5_out, Go_to_ground_ff2_q, Go_to_ground_ff_q);
  D_Flip_Flop Go_to_ground_ff (
    .clk(Clock_out), .D(floor_button_1_go_floor0_signal), .Q(Go_to_ground_ff_q));  // open: Qn, preset, en, reset
  D_Flip_Flop Go_to_2nd_floor_ff2 (
    .clk(Clock_out), .D(Go_to_2nd_floor_ff_q), .Q(Go_to_2nd_floor_ff2_q));  // open: Qn, preset, en, reset
  or or_6 (or_6_out, Go_to_2nd_floor_ff2_q, Go_to_2nd_floor_ff2_q, Go_to_2nd_floor_ff_q, Go_to_2nd_floor_ff_q, Go_to_2nd_floor_ff_q);
  D_Flip_Flop Go_to_2nd_floor_ff (
    .clk(Clock_out), .D(floor_button_1_go_floor2_signal), .Q(Go_to_2nd_floor_ff_q));  // open: Qn, preset, en, reset
  Elevator elevator_1 (
    .Ground_floor(Floor0_q), .Floor1(Floor1_q), .Floor2(Floor2_q), .Ground_Floor_button_press(or_1_out),
    .Floor1_button_press(or_4_out), .Floor2_button_press(or_2_out), .Ground_floor_sensor(or_5_out),
    .Floor1_sensor(or_3_out), .Floor2_sensor(or_6_out), .Ground_Floor_2(elevator_1_ground_floor_2),
    .Floor1_2(elevator_1_floor1_2), .Floor2_2(elevator_1_floor2_2), .Call_Button(elevator_1_call_button),
    .Door(elevator_1_door), .Upward(elevator_1_upward), .Downward(elevator_1_downward));
  LED _0 (.in(elevator_1_ground_floor_2));
  Decoder #(.enable("false")) decoder_1 (.out0(decoder_1_out0), .out1(decoder_1_out1), .sel(elevator_1_door));
  LED _1 (.in(elevator_1_floor1_2));
  LED _2 (.in(elevator_1_floor2_2));
  not not_1 (not_1_out, elevator_1_call_button);
  Decoder #(.enable("false")) decoder_2 (.out0(decoder_2_out0), .out1(decoder_2_out1), .sel(elevator_1_call_button));
  Display display_1 (
    .Floor0(elevator_1_ground_floor_2), .Floor1(elevator_1_floor1_2), .Floor2(elevator_1_floor2_2),
    .a(display_1_a), .b(display_1_b), .c(display_1_c), .d(display_1_d), .e(display_1_e), .f(display_1_f),
    .g(display_1_g), .Point(display_1_point));
  _7_Segment_Display u_7_segment_display_1 (
    .g(display_1_g), .f(display_1_f), .a(display_1_a), .b(display_1_b), .e(display_1_e), .d(display_1_d),
    .c(display_1_c), .dp(display_1_point));
  LED Up (.in(elevator_1_upward));
  LED Down (.in(elevator_1_downward));
  LED Ready (.in(not_1_out));
  LED Door_Closed (.in(decoder_1_out1));
  Button CALL_to_2nd (.out(CALL_to_2nd_out));
  Button CALL_to_1st (.out(CALL_to_1st_out));
  Button CALL_to_floor (.out(CALL_to_floor_out));
  LED Door_Open (.in(decoder_1_out0));
  LED Busy (.in(decoder_2_out1));
  LED Usable (.in(decoder_2_out0));
  Button Go_2nd (.out(Go_2nd_out));
  Button GO_1st (.out(GO_1st_out));
  Button GO_floor (.out(GO_floor_out));
  Floor_Button floor_button_1 (
    .Go_to_Floor2(Go_2nd_out), .Go_to_Floor1(GO_1st_out), .Go_to_Floor0(GO_floor_out),
    .Call_elevator_to_Floor2(CALL_to_2nd_out), .Call_elevator_to_floor1(CALL_to_1st_out),
    .call_elevator_to_Floor0(CALL_to_floor_out), .Go_Floor2_signal(floor_button_1_go_floor2_signal),
    .Go_Floor1_signal(floor_button_1_go_floor1_signal), .Go_Floor0_Signal(floor_button_1_go_floor0_signal),
    .Call_Floor2(floor_button_1_call_floor2), .Call_Floor1(floor_button_1_call_floor1),
    .Call_Floor0(floor_button_1_call_floor0));

  // Notes on the sheet:
  //   Flip Flop triggering
  //   Floor Holding Flip flop
  //   Decoders are for representing 2 states with a single bit
  //   Floor Display
  //   Initial value 0 floor recieved
endmodule

module Display (
  input  Floor0,
  input  Floor1,
  input  Floor2,
  output a,
  output b,
  output c,
  output d,
  output e,
  output f,
  output g,
  output Point
);

  wire and_1_out, and_2_out, and_3_out, and_4_out, and_5_out, and_6_out, and_7_out, and_8_out, and_9_out,
       and_10_out, and_11_out, not_1_out, not_2_out, not_3_out, not_4_out, not_5_out, not_6_out, not_7_out,
       not_8_out, not_9_out, not_10_out, not_11_out, not_12_out, not_13_out, not_14_out, not_15_out,
       not_16_out, not_17_out, not_18_out, not_19_out, not_20_out, not_21_out, not_22_out, not_23_out,
       not_24_out, not_25_out, not_26_out;

  not not_1 (not_1_out, Floor0);
  not not_2 (not_2_out, Floor1);
  not not_3 (not_3_out, Floor1);
  not not_4 (not_4_out, Floor2);
  not not_5 (not_5_out, Floor0);
  not not_6 (not_6_out, Floor1);
  not not_7 (not_7_out, Floor0);
  not not_8 (not_8_out, Floor2);
  not not_9 (not_9_out, Floor1);
  not not_10 (not_10_out, Floor2);
  not not_11 (not_11_out, Floor0);
  not not_12 (not_12_out, Floor2);
  not not_13 (not_13_out, Floor1);
  not not_14 (not_14_out, Floor2);
  not not_15 (not_15_out, Floor0);
  not not_16 (not_16_out, Floor1);
  not not_17 (not_17_out, Floor1);
  not not_18 (not_18_out, Floor2);
  not not_19 (not_19_out, Floor0);
  not not_20 (not_20_out, Floor1);
  not not_21 (not_21_out, Floor1);
  not not_22 (not_22_out, Floor2);
  not not_23 (not_23_out, Floor1);
  not not_24 (not_24_out, Floor2);
  not not_25 (not_25_out, Floor0);
  not not_26 (not_26_out, Floor1);
  and and_1 (and_1_out, not_1_out, not_2_out, Floor2);
  and and_2 (and_2_out, Floor0, not_3_out, not_4_out);
  and and_3 (and_3_out, not_5_out, not_6_out, Floor2);
  and and_4 (and_4_out, not_7_out, Floor1, not_8_out);
  and and_5 (and_5_out, Floor0, not_9_out, not_10_out);
  and and_6 (and_6_out, not_11_out, Floor1, not_12_out);
  and and_7 (and_7_out, Floor0, not_13_out, not_14_out);
  and and_8 (and_8_out, not_15_out, not_16_out, Floor2);
  and and_9 (and_9_out, Floor0, not_17_out, not_18_out);
  and and_10 (and_10_out, not_19_out, not_20_out, Floor2);
  and and_11 (and_11_out, Floor0, not_21_out, not_22_out);
  and and_12 (f, Floor0, not_23_out, not_24_out);
  and and_13 (g, not_25_out, not_26_out, Floor2);
  or or_1 (e, and_10_out, and_11_out);
  or or_2 (a, and_1_out, and_2_out);
  or or_3 (b, and_3_out, and_4_out, and_5_out);
  or or_4 (c, and_6_out, and_7_out);
  or or_5 (d, and_8_out, and_9_out);

  assign Point = 1'b1;
endmodule

module Elevator (
  input  Ground_floor,
  input  Floor1,
  input  Floor2,
  input  Ground_Floor_button_press,
  input  Floor1_button_press,
  input  Floor2_button_press,
  input  Ground_floor_sensor,
  input  Floor1_sensor,
  input  Floor2_sensor,
  output Ground_Floor_2,
  output Floor1_2,
  output Floor2_2,
  output Call_Button,
  output Door,
  output Upward,
  output Downward
);

  wire and_1_out, and_2_out, and_3_out, and_4_out, and_5_out, and_6_out, and_7_out, and_8_out, and_9_out,
       and_10_out, and_11_out, and_12_out, and_13_out, and_14_out, and_15_out, and_16_out, and_17_out,
       and_18_out, and_19_out, and_20_out, and_21_out, and_22_out, and_23_out, and_24_out, and_25_out,
       and_26_out, and_27_out, and_28_out, and_29_out, and_30_out, and_31_out, and_32_out, and_33_out,
       and_34_out, and_35_out, and_36_out, and_37_out, and_38_out, and_39_out, and_40_out, and_41_out,
       and_42_out, and_43_out, not_1_out, not_2_out, not_3_out, not_4_out, not_5_out, not_6_out, not_7_out,
       not_8_out, not_9_out, not_10_out, not_11_out, not_12_out, not_13_out, not_14_out, not_15_out,
       not_16_out, not_17_out, not_18_out, not_19_out, not_20_out, not_21_out, not_22_out, not_23_out,
       not_24_out, not_25_out, not_26_out, not_27_out, not_28_out, not_29_out, not_30_out, not_31_out,
       not_32_out, not_33_out, not_34_out, not_35_out, not_36_out, not_37_out, not_38_out, not_39_out,
       not_40_out, not_41_out, not_42_out;

  not not_1 (not_1_out, Floor1);
  not not_2 (not_2_out, Floor2);
  not not_3 (not_3_out, Floor1_button_press);
  not not_4 (not_4_out, Floor2_button_press);
  not not_5 (not_5_out, Floor1_sensor);
  not not_6 (not_6_out, Floor2_sensor);
  not not_7 (not_7_out, Floor2);
  not not_8 (not_8_out, Floor2);
  not not_9 (not_9_out, Ground_Floor_button_press);
  not not_10 (not_10_out, Floor2_button_press);
  not not_11 (not_11_out, Ground_floor_sensor);
  not not_12 (not_12_out, Floor2_sensor);
  not not_13 (not_13_out, Ground_floor);
  not not_14 (not_14_out, Ground_floor);
  not not_15 (not_15_out, Ground_Floor_button_press);
  not not_16 (not_16_out, Floor1_button_press);
  not not_17 (not_17_out, Ground_floor_sensor);
  not not_18 (not_18_out, Floor1_sensor);
  not not_19 (not_19_out, Floor2);
  not not_20 (not_20_out, Floor1);
  not not_21 (not_21_out, Ground_floor);
  not not_22 (not_22_out, Floor2);
  not not_23 (not_23_out, Floor1);
  not not_24 (not_24_out, Floor2);
  not not_25 (not_25_out, Floor1);
  not not_26 (not_26_out, Floor1);
  not not_27 (not_27_out, Floor2);
  not not_28 (not_28_out, Floor1);
  not not_29 (not_29_out, Floor2);
  not not_30 (not_30_out, Ground_floor);
  not not_31 (not_31_out, Floor2);
  not not_32 (not_32_out, Ground_Floor_button_press);
  not not_33 (not_33_out, Floor1_button_press);
  not not_34 (not_34_out, Ground_floor_sensor);
  not not_35 (not_35_out, Floor1_sensor);
  not not_36 (not_36_out, Floor1);
  not not_37 (not_37_out, Floor2);
  not not_38 (not_38_out, Floor1);
  not not_39 (not_39_out, Floor2);
  not not_40 (not_40_out, Ground_floor);
  not not_41 (not_41_out, Floor2_button_press);
  not not_42 (not_42_out, Floor2_sensor);
  and and_1 (and_1_out, not_1_out, not_2_out, not_3_out, not_4_out, not_5_out, not_6_out);
  and and_2 (and_2_out, not_7_out, Ground_floor_sensor);
  and and_3 (and_3_out, not_8_out, Ground_Floor_button_press);
  and and_4 (and_4_out, Floor2, Ground_floor_sensor);
  and and_5 (and_5_out, Floor2, Ground_Floor_button_press);
  and and_6 (and_6_out, Floor1, not_9_out, not_10_out, not_11_out, not_12_out);
  and and_7 (and_7_out, Ground_floor, Floor2_sensor);
  and and_8 (and_8_out, Ground_floor, Floor2_button_press);
  and and_9 (and_9_out, not_13_out, Floor2_sensor);
  and and_10 (and_10_out, not_14_out, Floor2_button_press);
  and and_11 (and_11_out, Floor2, not_15_out, not_16_out, not_17_out, not_18_out);
  and and_12 (and_12_out, not_19_out, Floor2_sensor);
  and and_13 (and_13_out, not_20_out, Floor1_sensor);
  and and_14 (and_14_out, not_21_out, Ground_floor_sensor);
  and and_15 (and_15_out, not_22_out, Floor2_button_press);
  and and_16 (and_16_out, not_23_out, Floor1_button_press);
  and and_17 (and_17_out, Floor2, Ground_Floor_button_press);
  and and_18 (and_18_out, Floor1, Ground_Floor_button_press);
  and and_19 (and_19_out, not_24_out, Floor2_sensor);
  and and_20 (and_20_out, not_25_out, Floor1_sensor);
  and and_21 (and_21_out, not_26_out, Floor1_button_press);
  and and_22 (and_22_out, Floor2, Ground_floor_sensor);
  and and_23 (and_23_out, Floor2, Ground_Floor_button_press);
  and and_24 (and_24_out, Floor1, Ground_floor_sensor);
  and and_25 (and_25_out, Floor1, Floor2_button_press);
  and and_26 (and_26_out, Floor1, Ground_Floor_button_press);
  and and_27 (and_27_out, Ground_floor, Floor2_button_press);
  and and_28 (and_28_out, not_27_out, Floor2_sensor);
  and and_29 (and_29_out, not_28_out, not_29_out, Floor1_sensor);
  and and_30 (and_30_out, not_30_out, not_31_out, not_32_out, not_33_out, Floor2_button_press, not_34_out, not_35_out);
  and and_31 (and_31_out, not_36_out, not_37_out, Floor2_button_press);
  and and_32 (and_32_out, not_38_out, not_39_out, Floor1_button_press);
  and and_33 (and_33_out, Floor2, Floor1_sensor);
  and and_34 (and_34_out, not_40_out, Floor2, not_41_out, Ground_floor_sensor, not_42_out);
  and and_35 (and_35_out, Floor2, Floor1_button_press);
  and and_36 (and_36_out, Floor2, Ground_Floor_button_press);
  and and_37 (and_37_out, Floor1, Ground_floor_sensor);
  and and_38 (and_38_out, Floor1, Floor2_button_press, Floor2_sensor);
  and and_39 (and_39_out, Floor1, Floor2_button_press, Floor1_sensor);
  and and_40 (and_40_out, Floor1, Floor1_button_press, Floor2_button_press);
  and and_41 (and_41_out, Floor1, Ground_Floor_button_press);
  and and_42 (and_42_out, Floor1, Floor2, Floor2_button_press);
  and and_43 (and_43_out, Ground_floor, Floor1, Floor2_button_press);
  or or_1 (Ground_Floor_2, and_1_out, and_2_out, and_3_out);
  or or_2 (Floor2_2, and_9_out, and_10_out, and_11_out);
  or or_3 (Call_Button, and_12_out, and_13_out, and_14_out, and_15_out, and_16_out, and_17_out, and_18_out);
  or or_4 (Door, and_19_out, and_20_out, and_21_out, and_22_out, and_23_out, and_24_out, and_25_out, and_26_out, and_27_out);
  or or_5 (Upward, and_28_out, and_29_out, and_30_out, and_31_out, and_32_out);
  or or_6 (Floor1_2, Floor1_sensor, Floor1_button_press, and_4_out, and_5_out, and_6_out, and_7_out, and_8_out);
  or or_7 (Downward, and_33_out, and_34_out, and_35_out, and_36_out, and_37_out, and_38_out, and_39_out, and_40_out, and_41_out, and_42_out, and_43_out);
endmodule

module Floor_Button (
  input  Go_to_Floor2,
  input  Go_to_Floor1,
  input  Go_to_Floor0,
  input  Call_elevator_to_Floor2,
  input  Call_elevator_to_floor1,
  input  call_elevator_to_Floor0,
  output Go_Floor2_signal,
  output Go_Floor1_signal,
  output Go_Floor0_Signal,
  output Call_Floor2,
  output Call_Floor1,
  output Call_Floor0
);

  wire clock_1_out;

  Clock clock_1 (.out(clock_1_out));
  D_Flip_Flop Go_to_Floor2_ff (
    .Q(Go_Floor2_signal), .preset(Go_to_Floor2), .reset(clock_1_out));  // open: clk, D, Qn, en
  D_Flip_Flop Go_to_Floor1_ff (
    .Q(Go_Floor1_signal), .preset(Go_to_Floor1), .reset(clock_1_out));  // open: clk, D, Qn, en
  D_Flip_Flop Go_to_Floor0_ff (
    .Q(Go_Floor0_Signal), .preset(Go_to_Floor0), .reset(clock_1_out));  // open: clk, D, Qn, en
  D_Flip_Flop Call_Floor2_ff (
    .Q(Call_Floor2), .preset(Call_elevator_to_Floor2), .reset(clock_1_out));  // open: clk, D, Qn, en
  D_Flip_Flop Call_Floor1_ff (
    .Q(Call_Floor1), .preset(Call_elevator_to_floor1), .reset(clock_1_out));  // open: clk, D, Qn, en
  D_Flip_Flop Call_Floor0_ff (
    .Q(Call_Floor0), .preset(call_elevator_to_Floor0), .reset(clock_1_out));  // open: clk, D, Qn, en
endmodule
